// Digital circuit day5.dig as structural Verilog
module day5 (
  input  B3,
  input  B2,
  input  B1,
  input  B0,
  input  clk,
  input  clr,
  input  b,
  input  a,
  input  set,
  output Z0,
  output Z1,
  output Z2,
  output Z3,
  output ready
);

  wire multiplexer_1_out, multiplexer_2_out, multiplexer_3_out, multiplexer_4_out;

  Multiplexer #(.Selector_Bits(2)) multiplexer_1 (
    .sel({a, b}), .in_0(1'b0), .in_1(B0), .in_2(B3), .in_3(B2), .out(multiplexer_1_out));
  D_FF_AS d_ff_as_1 (.Set(set), .D(multiplexer_1_out), .C(clk), .Clr(clr), .Q(Z0));  // open: nQ
  Multiplexer #(.Selector_Bits(2)) multiplexer_2 (
    .sel({a, b}), .in_0(1'b0), .in_1(B1), .in_2(B0), .in_3(B3), .out(multiplexer_2_out));
  D_FF_AS d_ff_as_2 (.Set(set), .D(multiplexer_2_out), .C(clk), .Clr(clr), .Q(Z1));  // open: nQ
  Multiplexer #(.Selector_Bits(2)) multiplexer_3 (
    .sel({a, b}), .in_0(1'b0), .in_1(B2), .in_2(B1), .in_3(B0), .out(multiplexer_3_out));
  D_FF_AS d_ff_as_3 (.Set(set), .D(multiplexer_3_out), .C(clk), .Clr(clr), .Q(Z2));  // open: nQ
  or or_1 (ready, Z3, Z2, Z1, Z0);
  Multiplexer #(.Selector_Bits(2)) multiplexer_4 (
    .sel({a, b}), .in_0(1'b0), .in_1(B3), .in_2(set), .in_3(B1), .out(multiplexer_4_out));
  D_FF_AS d_ff_as_4 (.Set(set), .D(multiplexer_4_out), .C(clk), .Clr(clr), .Q(Z3));  // open: nQ
endmodule
